// Logisim project pipelineCircuitFinal.circ as structural Verilog: 27 circuits, main circuit main
module main (
);

  wire ALU_zero, branchcontrol_1_branch, button_1_out, clock_1_out, Decoder_immtoalu, Decoder_immtopc,
       Decoder_led, Decoder_memread, Decoder_memtoreg, Decoder_memwrite, Decoder_regwrite, Decoder_writeled,
       Decoder_zerostoalu, EX_MEM_haltled_2, EX_MEM_memread, EX_MEM_readmemtoreg, EX_MEM_readmemwrite,
       EX_MEM_readregwrite, EX_MEM_writehex_2, halt_1_halt, ID_EX_haltled_2, ID_EX_memread, ID_EX_pausepc,
       ID_EX_readimmtoalu, ID_EX_readmemtoreg, ID_EX_readmemwrite, ID_EX_readregwrite, ID_EX_readzerostoalu,
       ID_EX_writehex_2, Instruction_Splitter_subop, Instruction_Splitter_unsigned, mem_wb_1_haltled_2,
       mem_wb_1_readmemtoreg, mem_wb_1_readregwrite, mem_wb_1_writehex_2, not_1_out, or_1_out,
       ResultToLess_less;
  wire [2:0] EX_MEM_readrs, EX_MEM_readrt, ID_EX_readrs, ID_EX_readrt, Instruction_Splitter_readregister1,
       Instruction_Splitter_readregister2, mem_wb_1_readrs;
  wire [3:0] Decoder_aluop, ID_EX_aluop, Instruction_Splitter_opcode, register_1_q;
  wire [7:0] adder_1_out, ID_EX_immnotextended_2, Instruction_Splitter_immediate, multiplexer_1_out, PC_q,
       RegistertoAddress_address;
  wire [15:0] ALU_result, EX_MEM_alu, EX_MEM_readregdata1, EX_MEM_readregdata2, ID_EX_readregdata1,
       ID_EX_readregdata2, ID_EX_readsignextend, IF_ID_readinstruction, mem_wb_1_alu, mem_wb_1_data1_2,
       mem_wb_1_memdata_2, memtoex_forward_1_rs_data, memtoex_forward_1_rt_data, multiplexer_2_out,
       multiplexer_3_out, multiplexer_4_out, ram_1_data, register_2_q, Registers_readdata1,
       Registers_readdata2, rom_1_data, Sign_Extend_signextendedimm;

  not not_1 (not_1_out, or_1_out);
  Clock clock_1 (.out(clock_1_out));
  or or_1 (or_1_out, halt_1_halt, ID_EX_pausepc);
  Register PC (.D(multiplexer_1_out), .en(not_1_out), .Q(PC_q), .clk(clock_1_out), .clr(button_1_out));
  Button button_1 (.out(button_1_out));
  Adder adder_1 (.a(PC_q), .b(8'h1), .out(adder_1_out));  // open: cin, cout
  ROM #(.dataWidth(16)) rom_1 (.addr(PC_q), .data(rom_1_data), .sel(1'b1));
  Halt halt_1 (.Instruction(rom_1_data), .Halt(halt_1_halt));  // open: Opcode
  IF_ID IF_ID (
    .ReadFromInstMemory(rom_1_data), .ReadInstruction(IF_ID_readinstruction), .Clock(clock_1_out),
    .Freeze(branchcontrol_1_branch), .op(register_1_q));
  InstructionSplitter Instruction_Splitter (
    .Instruction(IF_ID_readinstruction), .Opcode(Instruction_Splitter_opcode),
    .ReadRegister1(Instruction_Splitter_readregister1), .ReadRegister2(Instruction_Splitter_readregister2),
    .SubOp(Instruction_Splitter_subop), .Unsigned(Instruction_Splitter_unsigned),
    .Immediate(Instruction_Splitter_immediate));  // open: WriteRegister, ShiftAmount
  SignExtend Sign_Extend (
    .Unsigned(Instruction_Splitter_unsigned), .Immediate(Instruction_Splitter_immediate),
    .SignExtendedImm(Sign_Extend_signextendedimm));
  ResultToLess ResultToLess (.Result(ALU_result), .Less(ResultToLess_less));
  RegisterFile Registers (
    .ReadRegister1(Instruction_Splitter_readregister1), .ReadRegister2(Instruction_Splitter_readregister2),
    .WriteRegister(mem_wb_1_readrs), .WriteData(multiplexer_4_out), .WriteEnable(mem_wb_1_readregwrite),
    .Clock(clock_1_out), .ReadData1(Registers_readdata1), .ReadData2(Registers_readdata2));
  Decoder Decoder (
    .Opcode(Instruction_Splitter_opcode), .Subop(Instruction_Splitter_subop), .Zero(ALU_zero),
    .Less(ResultToLess_less), .RegWrite(Decoder_regwrite), .ALUOp(Decoder_aluop),
    .IMMtoALU(Decoder_immtoalu), .IMMtoPC(Decoder_immtopc), .ZerosToALU(Decoder_zerostoalu),
    .MemWrite(Decoder_memwrite), .MemtoReg(Decoder_memtoreg), .LED(Decoder_led), .WriteLED(Decoder_writeled),
    .MemRead(Decoder_memread));  // open: ShiftSrc, ShifterToReg, RegtoPC, Halt, PCtoReg
  branchControl branchcontrol_1 (.Opcode(register_1_q), .Zero(ALU_zero), .branch(branchcontrol_1_branch));
  Register #(.width(4)) register_1 (
    .D(Instruction_Splitter_opcode), .Q(register_1_q), .clk(clock_1_out));  // open: en, clr
  ID_EX ID_EX (
    .ReadFromRegWrite(Decoder_regwrite), .ReadFromALUOp(Decoder_aluop), .ReadFromImmToALU(Decoder_immtoalu),
    .ReadFromImmToPC(Decoder_immtopc), .ReadFromZerosToALU(Decoder_zerostoalu),
    .ReadFromMemWrite(Decoder_memwrite), .ReadFromMemToReg(Decoder_memtoreg), .HaltLED(Decoder_led),
    .WriteHex(Decoder_writeled), .ReadFromMemRead(Decoder_memread),
    .ImmNotExtended(Instruction_Splitter_immediate), .ReadFromRegData1(Registers_readdata1),
    .ReadFromRegData2(Registers_readdata2), .ReadFromSignExtend(Sign_Extend_signextendedimm),
    .Rs(Instruction_Splitter_readregister1), .ReadRegWRite(ID_EX_readregwrite), .ALUOp(ID_EX_aluop),
    .ReadImmToALU(ID_EX_readimmtoalu), .ReadZerosToALU(ID_EX_readzerostoalu),
    .ReadMemWrite(ID_EX_readmemwrite), .ReadMemToReg(ID_EX_readmemtoreg), .HaltLED_2(ID_EX_haltled_2),
    .WriteHex_2(ID_EX_writehex_2), .MemRead(ID_EX_memread), .ImmNotExtended_2(ID_EX_immnotextended_2),
    .ReadRegData1(ID_EX_readregdata1), .ReadRegData2(ID_EX_readregdata2),
    .ReadSignExtend(ID_EX_readsignextend), .ReadRs(ID_EX_readrs), .Clock(clock_1_out),
    .Rt(Instruction_Splitter_readregister2), .ReadRt(ID_EX_readrt), .Rd(mem_wb_1_readrs),
    .WB_RegWrite(mem_wb_1_readregwrite), .WB_WriteData(multiplexer_4_out), .PausePC(ID_EX_pausepc),
    .BranchTaken(branchcontrol_1_branch));  // open: ReadImmToPC
  Multiplexer #(.width(8), .disabled(0), .enable("false")) multiplexer_1 (
    .in0(adder_1_out), .in1(ID_EX_immnotextended_2), .out(multiplexer_1_out), .sel(branchcontrol_1_branch));
  Register #(.width(16)) register_2 (
    .D(mem_wb_1_data1_2), .en(mem_wb_1_writehex_2), .Q(register_2_q), .clk(clock_1_out));  // open: clr
  Hex_Digit_Display hex_digit_display_1 (.value(register_2_q[15:12]));  // open: dp
  Hex_Digit_Display hex_digit_display_2 (.value(register_2_q[11:8]));  // open: dp
  MemToEx_Forward memtoex_forward_1 (
    .IdEx_RsData(ID_EX_readregdata1), .ExMemAlu(EX_MEM_alu), .MemWB_Data(multiplexer_4_out),
    .IdEx_Rs(ID_EX_readrs), .MemWB_Rs(mem_wb_1_readrs), .MemWB_RegWrite(mem_wb_1_readregwrite),
    .IdEx_Rs_2(ID_EX_readrs), .ExMem_Rs(EX_MEM_readrs), .ExMem_RegWrite(EX_MEM_readregwrite),
    .Rs_Data(memtoex_forward_1_rs_data), .IdEx_Rt(ID_EX_readrt), .Rt_Data(memtoex_forward_1_rt_data),
    .IdEx_RtData(ID_EX_readregdata2), .ExMem_MemToReg(EX_MEM_readmemtoreg),
    .MemWB_MemToReg(mem_wb_1_readmemtoreg));
  Multiplexer #(.width(16), .disabled(0), .enable("false")) multiplexer_2 (
    .in0(memtoex_forward_1_rt_data), .in1(ID_EX_readsignextend), .out(multiplexer_2_out),
    .sel(ID_EX_readimmtoalu));
  Multiplexer #(.width(16), .disabled(0), .enable("false")) multiplexer_3 (
    .in0(multiplexer_2_out), .in1({16{1'b0}}), .out(multiplexer_3_out), .sel(ID_EX_readzerostoalu));
  Hex_Digit_Display hex_digit_display_3 (.value(register_2_q[7:4]));  // open: dp
  Hex_Digit_Display hex_digit_display_4 (.value(register_2_q[3:0]));  // open: dp
  sixteen_bit_ALU ALU (
    .ALUOperation(ID_EX_aluop), .a(memtoex_forward_1_rs_data), .b(multiplexer_3_out), .Zero(ALU_zero),
    .Result(ALU_result));  // open: Overflow
  LED Halt_2 (.in(mem_wb_1_haltled_2));
  EX_MEM EX_MEM (
    .ReadFromMemToReg(ID_EX_readmemtoreg), .ReadFromRegWrite(ID_EX_readregwrite), .HaltLED(ID_EX_haltled_2),
    .ReadFromMemWrite(ID_EX_readmemwrite), .ReadFromMemRead(ID_EX_memread), .ReadFromALU(ALU_result),
    .ReadFromRegData2(ID_EX_readregdata2), .Rs(ID_EX_readrs), .Rt(ID_EX_readrt),
    .ReadMemToReg(EX_MEM_readmemtoreg), .ReadRegWRite(EX_MEM_readregwrite), .HaltLED_2(EX_MEM_haltled_2),
    .ReadMemWrite(EX_MEM_readmemwrite), .MemRead(EX_MEM_memread), .ALU(EX_MEM_alu),
    .ReadRegData2(EX_MEM_readregdata2), .ReadRs(EX_MEM_readrs), .ReadRt(EX_MEM_readrt), .Clock(clock_1_out),
    .ReadFromRegData1(memtoex_forward_1_rs_data), .ReadRegData1(EX_MEM_readregdata1),
    .WriteHex(ID_EX_writehex_2), .WriteHex_2(EX_MEM_writehex_2));
  ALUtoPC RegistertoAddress (.ALUOut(EX_MEM_readregdata2), .Address(RegistertoAddress_address));
  RAM #(.dataWidth(16), .bus("separate")) ram_1 (
    .addr(RegistertoAddress_address), .din(EX_MEM_readregdata1), .data(ram_1_data),
    .str(EX_MEM_readmemwrite), .sel(1'b1), .clk(clock_1_out), .ld(EX_MEM_memread));  // open: clr
  MEM_WB mem_wb_1 (
    .ReadFromMemToReg(EX_MEM_readmemtoreg), .ReadFromRegWrite(EX_MEM_readregwrite),
    .HaltLED(EX_MEM_haltled_2), .ReadFromALU(EX_MEM_alu), .MemData(ram_1_data), .Rs(EX_MEM_readrs),
    .Rt(EX_MEM_readrt), .WriteHEx(EX_MEM_writehex_2), .Data1(EX_MEM_readregdata1), .Clock(clock_1_out),
    .ReadMemToReg(mem_wb_1_readmemtoreg), .ReadRegWRite(mem_wb_1_readregwrite),
    .HaltLED_2(mem_wb_1_haltled_2), .ALU(mem_wb_1_alu), .MemData_2(mem_wb_1_memdata_2),
    .ReadRs(mem_wb_1_readrs), .WriteHEx_2(mem_wb_1_writehex_2), .Data1_2(mem_wb_1_data1_2));  // open: ReadRt
  Multiplexer #(.width(16), .disabled(0), .enable("false")) multiplexer_4 (
    .in0(mem_wb_1_alu), .in1(mem_wb_1_memdata_2), .out(multiplexer_4_out), .sel(mem_wb_1_readmemtoreg));

  // Notes on the sheet:
  //   contents of rom_1 (hex, n*v repeats v):
  //   280 8605 1402 1904 a206 1c06 1a07 f400 f200 f600 fc00 7000
endmodule

module InstructionSplitter (
  input  [15:0] Instruction,
  output [3:0] Opcode,
  output [2:0] ReadRegister1,
  output [2:0] ReadRegister2,
  output [2:0] WriteRegister,
  output [3:0] ShiftAmount,
  output SubOp,
  output Unsigned,
  output [7:0] Immediate
);


  assign Immediate = Instruction[7:0];
  assign Opcode = Instruction[15:12];
  assign ReadRegister1 = Instruction[11:9];
  assign ReadRegister2 = Instruction[8:6];
  assign ShiftAmount = Instruction[4:1];
  assign SubOp = Instruction[0];
  assign Unsigned = Instruction[8];
  assign WriteRegister = Instruction[11:9];
endmodule

module SignExtend (
  input  Unsigned,
  input  [7:0] Immediate,
  output [15:0] SignExtendedImm
);

  wire [15:0] bit_extender_1_out, bit_extender_2_out;

  assign bit_extender_1_out = {{8{Immediate[7]}}, Immediate};  // Bit_Extender bit_extender_1
  assign bit_extender_2_out = {{8{1'b0}}, Immediate};  // Bit_Extender bit_extender_2
  Multiplexer #(.width(16), .disabled(0), .enable("false")) multiplexer_1 (
    .in0(bit_extender_1_out), .in1(bit_extender_2_out), .out(SignExtendedImm), .sel(Unsigned));
endmodule

module ALUtoPC (
  input  [15:0] ALUOut,
  output [7:0] Address
);


  assign Address = ALUOut[7:0];
endmodule

module Shifter (
  input  Subop,
  input  [15:0] Data,
  input  [15:0] ShamtReg,
  input  ShiftSrc,
  input  [3:0] Shamt,
  output [15:0] ShiftOut
);

  wire [3:0] multiplexer_1_out;
  wire [15:0] shifter_1_out, shifter_2_out;

  Multiplexer #(.width(4), .disabled(0), .enable("false")) multiplexer_1 (
    .in0(ShamtReg[3:0]), .in1(Shamt), .out(multiplexer_1_out), .sel(ShiftSrc));
  Shifter_part #(.width(16)) shifter_1 (.in(Data), .\dist (multiplexer_1_out), .out(shifter_1_out));
  Shifter_part #(.width(16), .shift("lr")) shifter_2 (.in(Data), .\dist (multiplexer_1_out), .out(shifter_2_out));
  Multiplexer #(.width(16), .disabled(0), .enable("false")) multiplexer_2 (
    .in0(shifter_1_out), .in1(shifter_2_out), .out(ShiftOut), .sel(Subop));
endmodule

module RegisterFile (
  input  [2:0] ReadRegister1,
  input  [2:0] ReadRegister2,
  input  [2:0] WriteRegister,
  input  [15:0] WriteData,
  input  WriteEnable,
  input  Clock,
  output [15:0] ReadData1,
  output [15:0] ReadData2
);

  wire decoder_1_out0, decoder_1_out1, decoder_1_out2, decoder_1_out3, decoder_1_out4, decoder_1_out5,
       decoder_1_out6, decoder_1_out7;
  wire [15:0] register_1_q, register_2_q, register_3_q, register_4_q, register_5_q, register_6_q,
       register_7_q, register_8_q;

  Decoder_part #(.select(3), .disabled(0)) decoder_1 (
    .out0(decoder_1_out0), .out1(decoder_1_out1), .out2(decoder_1_out2), .out3(decoder_1_out3),
    .out4(decoder_1_out4), .out5(decoder_1_out5), .out6(decoder_1_out6), .out7(decoder_1_out7),
    .sel(WriteRegister), .en(WriteEnable));
  Register #(.width(16)) register_1 (.D(WriteData), .en(decoder_1_out0), .Q(register_1_q), .clk(Clock));  // open: clr
  Register #(.width(16)) register_2 (.D(WriteData), .en(decoder_1_out1), .Q(register_2_q), .clk(Clock));  // open: clr
  Register #(.width(16)) register_3 (.D(WriteData), .en(decoder_1_out2), .Q(register_3_q), .clk(Clock));  // open: clr
  Register #(.width(16)) register_4 (.D(WriteData), .en(decoder_1_out3), .Q(register_4_q), .clk(Clock));  // open: clr
  Register #(.width(16)) register_5 (.D(WriteData), .en(decoder_1_out4), .Q(register_5_q), .clk(Clock));  // open: clr
  Register #(.width(16)) register_6 (.D(WriteData), .en(decoder_1_out5), .Q(register_6_q), .clk(Clock));  // open: clr
  Register #(.width(16)) register_7 (.D(WriteData), .en(decoder_1_out6), .Q(register_7_q), .clk(Clock));  // open: clr
  Register #(.width(16)) register_8 (.D(WriteData), .en(decoder_1_out7), .Q(register_8_q), .clk(Clock));  // open: clr
  Multiplexer #(.select(3), .width(16), .enable("false")) multiplexer_1 (
    .in0(register_1_q), .in1(register_2_q), .in2(register_3_q), .in3(register_4_q), .in4(register_5_q),
    .in5(register_6_q), .in6(register_7_q), .in7(register_8_q), .out(ReadData1), .sel(ReadRegister1));
  Multiplexer #(.select(3), .width(16), .enable("false")) multiplexer_2 (
    .in0(register_1_q), .in1(register_2_q), .in2(register_3_q), .in3(register_4_q), .in4(register_5_q),
    .in5(register_6_q), .in6(register_7_q), .in7(register_8_q), .out(ReadData2), .sel(ReadRegister2));
endmodule

module ShifterDecoder (
  input  [3:0] Opcode,
  output ShiftSrc,
  output ShiftertoReg,
  output RegWrite
);

  and and_1 (RegWrite, ~Opcode[3], Opcode[2], ~Opcode[1]);  // AND_Gate

  assign ShiftertoReg = RegWrite;
  assign ShiftSrc = Opcode[0];
endmodule

module Arith_Log_Decoder (
  input  [3:0] Opcode,
  input  Subop,
  output [3:0] ALUOperation,
  output RegWrite,
  output ALUSrc
);

  wire and_2_out, and_3_out, and_5_out, and_6_out, not_1_out, not_2_out, not_3_out, not_4_out, not_5_out,
       not_6_out, not_7_out, not_8_out, not_9_out, not_10_out, not_11_out, not_12_out, not_13_out,
       not_14_out, not_15_out, not_16_out, not_17_out, not_18_out, not_19_out, not_20_out, not_21_out;

  not not_1 (not_1_out, Opcode[3]);
  not not_2 (not_2_out, Opcode[2]);
  not not_3 (not_3_out, Subop);
  not not_4 (not_4_out, Opcode[3]);
  not not_5 (not_5_out, Opcode[2]);
  not not_6 (not_6_out, Opcode[1]);
  not not_7 (not_7_out, Opcode[0]);
  not not_8 (not_8_out, Opcode[3]);
  not not_9 (not_9_out, Opcode[2]);
  not not_10 (not_10_out, Subop);
  not not_11 (not_11_out, Opcode[3]);
  not not_12 (not_12_out, Opcode[2]);
  not not_13 (not_13_out, Opcode[1]);
  not not_14 (not_14_out, Opcode[3]);
  not not_15 (not_15_out, Opcode[2]);
  not not_16 (not_16_out, Opcode[1]);
  not not_17 (not_17_out, Opcode[3]);
  not not_18 (not_18_out, Opcode[2]);
  not not_19 (not_19_out, Opcode[3]);
  not not_20 (not_20_out, Opcode[2]);
  not not_21 (not_21_out, Opcode[1]);
  and and_1 (ALUOperation[3], not_1_out, not_2_out, Opcode[1], Opcode[0], not_3_out);
  and and_2 (and_2_out, not_4_out, not_5_out, not_6_out, not_7_out, Subop);
  and and_3 (and_3_out, not_8_out, not_9_out, Opcode[1], Opcode[0], not_10_out);
  and and_4 (ALUOperation[1], not_11_out, not_12_out, not_13_out);
  and and_5 (and_5_out, not_14_out, not_15_out, not_16_out);
  and and_6 (and_6_out, not_17_out, not_18_out, Opcode[0]);
  and and_7 (ALUSrc, not_19_out, not_20_out, not_21_out, Opcode[0]);
  or or_1 (ALUOperation[2], and_2_out, and_3_out);
  or or_2 (RegWrite, and_5_out, and_6_out);

  assign ALUOperation[0] = 1'b0;
endmodule

module Arith_Log (
  input  Opcode3,
  input  Opcode2,
  input  Opcode1,
  input  Opcode0,
  input  Unsigned,
  input  Subop,
  output ALUOp3,
  output ALUOp2,
  output ALUOp1,
  output ALUOp0,
  output RegWrite,
  output ALUSrc
);

  wire and_2_out, and_3_out, and_5_out, and_6_out, not_1_out, not_2_out, not_3_out, not_4_out, not_5_out,
       not_6_out, not_7_out, not_8_out, not_9_out, not_10_out, not_11_out, not_12_out, not_13_out,
       not_14_out, not_15_out, not_16_out, not_17_out, not_18_out, not_19_out, not_20_out, not_21_out;

  not not_1 (not_1_out, Opcode3);
  not not_2 (not_2_out, Opcode2);
  not not_3 (not_3_out, Subop);
  not not_4 (not_4_out, Opcode3);
  not not_5 (not_5_out, Opcode2);
  not not_6 (not_6_out, Opcode1);
  not not_7 (not_7_out, Opcode0);
  not not_8 (not_8_out, Opcode3);
  not not_9 (not_9_out, Opcode2);
  not not_10 (not_10_out, Subop);
  not not_11 (not_11_out, Opcode3);
  not not_12 (not_12_out, Opcode2);
  not not_13 (not_13_out, Opcode1);
  not not_14 (not_14_out, Opcode3);
  not not_15 (not_15_out, Opcode2);
  not not_16 (not_16_out, Opcode1);
  not not_17 (not_17_out, Opcode3);
  not not_18 (not_18_out, Opcode2);
  not not_19 (not_19_out, Opcode3);
  not not_20 (not_20_out, Opcode2);
  not not_21 (not_21_out, Opcode1);
  and and_1 (ALUOp3, not_1_out, not_2_out, Opcode1, Opcode0, not_3_out);
  and and_2 (and_2_out, not_4_out, not_5_out, not_6_out, not_7_out, Subop);
  and and_3 (and_3_out, not_8_out, not_9_out, Opcode1, Opcode0, not_10_out);
  and and_4 (ALUOp1, not_11_out, not_12_out, not_13_out);
  and and_5 (and_5_out, not_14_out, not_15_out, not_16_out);
  and and_6 (and_6_out, not_17_out, not_18_out, Opcode0);
  and and_7 (ALUSrc, not_19_out, not_20_out, not_21_out, Opcode0);
  or or_1 (ALUOp2, and_2_out, and_3_out);
  or or_2 (RegWrite, and_5_out, and_6_out);

  assign ALUOp0 = 1'b0;
endmodule

module one_bit_ALU (
  input  Ainvert,
  input  Binvert,
  input  CarryIn,
  input  [1:0] Operation,
  input  a,
  input  b,
  input  Less,
  output Result,
  output Set,
  output CarryOut
);

  wire and_1_out, multiplexer_1_out, multiplexer_2_out, not_1_out, not_2_out, or_1_out;

  not not_1 (not_1_out, a);
  Multiplexer #(.enable("false")) multiplexer_1 (.in0(a), .in1(not_1_out), .out(multiplexer_1_out), .sel(Ainvert));
  not not_2 (not_2_out, b);
  Multiplexer #(.enable("false")) multiplexer_2 (.in0(b), .in1(not_2_out), .out(multiplexer_2_out), .sel(Binvert));
  and and_1 (and_1_out, multiplexer_1_out, multiplexer_2_out);
  or or_1 (or_1_out, multiplexer_1_out, multiplexer_2_out);
  Adder #(.width(1)) adder_1 (.a(multiplexer_1_out), .b(multiplexer_2_out), .out(Set), .cin(CarryIn), .cout(CarryOut));
  Multiplexer #(.select(2), .enable("false")) multiplexer_3 (
    .in0(and_1_out), .in1(or_1_out), .in2(Set), .in3(Less), .out(Result), .sel(Operation));
endmodule

module sixteen_bit_ALU (
  input  [3:0] ALUOperation,
  input  [15:0] a,
  input  [15:0] b,
  output Zero,
  output [15:0] Result,
  output Overflow
);

  wire comparator_1_eq, one_bit_alu_1_carryout, one_bit_alu_2_carryout, one_bit_alu_3_carryout,
       one_bit_alu_4_carryout, one_bit_alu_5_carryout, one_bit_alu_6_carryout, one_bit_alu_7_carryout,
       one_bit_alu_8_carryout, one_bit_alu_9_carryout, one_bit_alu_10_carryout, one_bit_alu_11_carryout,
       one_bit_alu_12_carryout, one_bit_alu_13_carryout, one_bit_alu_14_carryout, one_bit_alu_15_carryout,
       one_bit_alu_16_carryout, one_bit_alu_16_set, xor_1_out;
  wire [15:0] multiplier_1_out, one_bit_alu_1_result;

  one_bit_ALU one_bit_alu_1 (
    .a(a[0]), .b(b[0]), .Less(xor_1_out), .Ainvert(ALUOperation[3]), .Binvert(ALUOperation[2]),
    .CarryIn(ALUOperation[2]), .Operation(ALUOperation[1:0]), .CarryOut(one_bit_alu_1_carryout),
    .Result(one_bit_alu_1_result[0]));  // open: Set
  one_bit_ALU one_bit_alu_2 (
    .a(a[1]), .b(b[1]), .Less(1'b0), .Ainvert(ALUOperation[3]), .Binvert(ALUOperation[2]),
    .CarryIn(one_bit_alu_1_carryout), .Operation(ALUOperation[1:0]), .CarryOut(one_bit_alu_2_carryout),
    .Result(one_bit_alu_1_result[1]));  // open: Set
  one_bit_ALU one_bit_alu_3 (
    .a(a[2]), .b(b[2]), .Less(1'b0), .Ainvert(ALUOperation[3]), .Binvert(ALUOperation[2]),
    .CarryIn(one_bit_alu_2_carryout), .Operation(ALUOperation[1:0]), .CarryOut(one_bit_alu_3_carryout),
    .Result(one_bit_alu_1_result[2]));  // open: Set
  one_bit_ALU one_bit_alu_4 (
    .a(a[3]), .b(b[3]), .Less(1'b0), .Ainvert(ALUOperation[3]), .Binvert(ALUOperation[2]),
    .CarryIn(one_bit_alu_3_carryout), .Operation(ALUOperation[1:0]), .CarryOut(one_bit_alu_4_carryout),
    .Result(one_bit_alu_1_result[3]));  // open: Set
  one_bit_ALU one_bit_alu_5 (
    .a(a[4]), .b(b[4]), .Less(1'b0), .Ainvert(ALUOperation[3]), .Binvert(ALUOperation[2]),
    .CarryIn(one_bit_alu_4_carryout), .Operation(ALUOperation[1:0]), .CarryOut(one_bit_alu_5_carryout),
    .Result(one_bit_alu_1_result[4]));  // open: Set
  one_bit_ALU one_bit_alu_6 (
    .a(a[5]), .b(b[5]), .Less(1'b0), .Ainvert(ALUOperation[3]), .Binvert(ALUOperation[2]),
    .CarryIn(one_bit_alu_5_carryout), .Operation(ALUOperation[1:0]), .CarryOut(one_bit_alu_6_carryout),
    .Result(one_bit_alu_1_result[5]));  // open: Set
  one_bit_ALU one_bit_alu_7 (
    .a(a[6]), .b(b[6]), .Less(1'b0), .Ainvert(ALUOperation[3]), .Binvert(ALUOperation[2]),
    .CarryIn(one_bit_alu_6_carryout), .Operation(ALUOperation[1:0]), .CarryOut(one_bit_alu_7_carryout),
    .Result(one_bit_alu_1_result[6]));  // open: Set
  one_bit_ALU one_bit_alu_8 (
    .a(a[7]), .b(b[7]), .Less(1'b0), .Ainvert(ALUOperation[3]), .Binvert(ALUOperation[2]),
    .CarryIn(one_bit_alu_7_carryout), .Operation(ALUOperation[1:0]), .CarryOut(one_bit_alu_8_carryout),
    .Result(one_bit_alu_1_result[7]));  // open: Set
  one_bit_ALU one_bit_alu_9 (
    .a(a[8]), .b(b[8]), .Less(1'b0), .Ainvert(ALUOperation[3]), .Binvert(ALUOperation[2]),
    .CarryIn(one_bit_alu_8_carryout), .Operation(ALUOperation[1:0]), .CarryOut(one_bit_alu_9_carryout),
    .Result(one_bit_alu_1_result[8]));  // open: Set
  one_bit_ALU one_bit_alu_10 (
    .a(a[9]), .b(b[9]), .Less(1'b0), .Ainvert(ALUOperation[3]), .Binvert(ALUOperation[2]),
    .CarryIn(one_bit_alu_9_carryout), .Operation(ALUOperation[1:0]), .CarryOut(one_bit_alu_10_carryout),
    .Result(one_bit_alu_1_result[9]));  // open: Set
  one_bit_ALU one_bit_alu_11 (
    .a(a[10]), .b(b[10]), .Less(1'b0), .Ainvert(ALUOperation[3]), .Binvert(ALUOperation[2]),
    .CarryIn(one_bit_alu_10_carryout), .Operation(ALUOperation[1:0]), .CarryOut(one_bit_alu_11_carryout),
    .Result(one_bit_alu_1_result[10]));  // open: Set
  one_bit_ALU one_bit_alu_12 (
    .a(a[11]), .b(b[11]), .Less(1'b0), .Ainvert(ALUOperation[3]), .Binvert(ALUOperation[2]),
    .CarryIn(one_bit_alu_11_carryout), .Operation(ALUOperation[1:0]), .CarryOut(one_bit_alu_12_carryout),
    .Result(one_bit_alu_1_result[11]));  // open: Set
  one_bit_ALU one_bit_alu_13 (
    .a(a[12]), .b(b[12]), .Less(1'b0), .Ainvert(ALUOperation[3]), .Binvert(ALUOperation[2]),
    .CarryIn(one_bit_alu_12_carryout), .Operation(ALUOperation[1:0]), .CarryOut(one_bit_alu_13_carryout),
    .Result(one_bit_alu_1_result[12]));  // open: Set
  one_bit_ALU one_bit_alu_14 (
    .a(a[13]), .b(b[13]), .Less(1'b0), .Ainvert(ALUOperation[3]), .Binvert(ALUOperation[2]),
    .CarryIn(one_bit_alu_13_carryout), .Operation(ALUOperation[1:0]), .CarryOut(one_bit_alu_14_carryout),
    .Result(one_bit_alu_1_result[13]));  // open: Set
  one_bit_ALU one_bit_alu_15 (
    .a(a[14]), .b(b[14]), .Less(1'b0), .Ainvert(ALUOperation[3]), .Binvert(ALUOperation[2]),
    .CarryIn(one_bit_alu_14_carryout), .Operation(ALUOperation[1:0]), .CarryOut(one_bit_alu_15_carryout),
    .Result(one_bit_alu_1_result[14]));  // open: Set
  one_bit_ALU one_bit_alu_16 (
    .a(a[15]), .b(b[15]), .Less(1'b0), .Ainvert(ALUOperation[3]), .Binvert(ALUOperation[2]),
    .CarryIn(one_bit_alu_15_carryout), .Operation(ALUOperation[1:0]), .CarryOut(one_bit_alu_16_carryout),
    .Result(one_bit_alu_1_result[15]), .Set(one_bit_alu_16_set));
  xor xor_1 (xor_1_out, one_bit_alu_16_set, Overflow);
  xor xor_2 (Overflow, one_bit_alu_15_carryout, one_bit_alu_16_carryout);
  nor nor_1 (Zero, one_bit_alu_1_result[0], one_bit_alu_1_result[1], one_bit_alu_1_result[2], one_bit_alu_1_result[3], one_bit_alu_1_result[4], one_bit_alu_1_result[5], one_bit_alu_1_result[6], one_bit_alu_1_result[7], one_bit_alu_1_result[8], one_bit_alu_1_result[9], one_bit_alu_1_result[10], one_bit_alu_1_result[11], one_bit_alu_1_result[12], one_bit_alu_1_result[13], one_bit_alu_1_result[14], one_bit_alu_1_result[15]);
  Multiplier #(.width(16)) multiplier_1 (.a(a), .b(b), .out(multiplier_1_out));  // open: cin, cout
  Multiplexer #(.width(16), .enable("false")) multiplexer_1 (
    .in0(one_bit_alu_1_result), .in1(multiplier_1_out), .out(Result), .sel(comparator_1_eq));
  Comparator #(.width(4)) comparator_1 (.a(ALUOperation), .b(4'b1111), .eq(comparator_1_eq));  // open: gt, lt
endmodule

module PCDecoder (
  input  [3:0] Opcode,
  input  Subop,
  input  Zero,
  input  Less,
  output RegtoPC,
  output IMMtoPC,
  output ZerosToALU,
  output [3:0] ALUOp
);

  wire and_4_out, and_5_out, and_6_out, and_7_out, and_8_out, not_1_out, not_2_out, not_3_out, not_4_out,
       not_5_out, not_6_out, not_7_out, not_8_out, not_9_out, not_10_out, not_11_out, not_12_out, not_13_out,
       not_14_out, not_15_out, not_16_out;

  not not_1 (not_1_out, Opcode[2]);
  not not_2 (not_2_out, Opcode[1]);
  not not_3 (not_3_out, Subop);
  not not_4 (not_4_out, Opcode[2]);
  not not_5 (not_5_out, Opcode[1]);
  not not_6 (not_6_out, Opcode[0]);
  not not_7 (not_7_out, Opcode[2]);
  not not_8 (not_8_out, Opcode[1]);
  not not_9 (not_9_out, Zero);
  not not_10 (not_10_out, Opcode[2]);
  not not_11 (not_11_out, Zero);
  not not_12 (not_12_out, Opcode[0]);
  not not_13 (not_13_out, Zero);
  not not_14 (not_14_out, Less);
  not not_15 (not_15_out, Opcode[0]);
  and and_1 (ZerosToALU, Opcode[3], not_16_out);
  not not_16 (not_16_out, Opcode[2]);
  and and_2 (ALUOp[1], Opcode[3], not_1_out);
  and and_3 (RegtoPC, Opcode[3], Opcode[2], not_2_out, Opcode[0], not_3_out);
  and and_4 (and_4_out, Opcode[3], not_4_out, not_5_out, not_6_out, Zero);
  and and_5 (and_5_out, Opcode[3], not_7_out, not_8_out, Opcode[0], not_9_out);
  and and_6 (and_6_out, Opcode[3], not_10_out, Opcode[0], not_11_out, Less);
  and and_7 (and_7_out, Opcode[3], Opcode[1], not_12_out, not_13_out, not_14_out);
  and and_8 (and_8_out, Opcode[3], Opcode[2], Opcode[1], not_15_out);
  or or_1 (IMMtoPC, and_4_out, and_5_out, and_6_out, and_7_out, and_8_out);

  assign {ALUOp[3:2], ALUOp[0]} = 3'b000;
endmodule

module PCDecoderLogic (
  input  Opcode3,
  input  Opcode2,
  input  Opcode1,
  input  Opcode0,
  input  Subop,
  input  Zero,
  input  Less,
  output RegtoPC,
  output IMMtoPC,
  output OnestoALU
);

  wire and_2_out, and_3_out, and_4_out, and_5_out, and_6_out, not_1_out, not_2_out, not_3_out, not_4_out,
       not_5_out, not_6_out, not_7_out, not_8_out, not_9_out, not_10_out, not_11_out, not_12_out, not_13_out,
       not_14_out, not_15_out;

  not not_1 (not_1_out, Opcode1);
  not not_2 (not_2_out, Subop);
  not not_3 (not_3_out, Opcode2);
  not not_4 (not_4_out, Opcode1);
  not not_5 (not_5_out, Opcode0);
  not not_6 (not_6_out, Opcode2);
  not not_7 (not_7_out, Opcode1);
  not not_8 (not_8_out, Zero);
  not not_9 (not_9_out, Opcode2);
  not not_10 (not_10_out, Zero);
  not not_11 (not_11_out, Opcode0);
  not not_12 (not_12_out, Zero);
  not not_13 (not_13_out, Less);
  not not_14 (not_14_out, Opcode0);
  not not_15 (not_15_out, Opcode2);
  and and_1 (RegtoPC, Opcode3, Opcode2, not_1_out, Opcode0, not_2_out);
  and and_2 (and_2_out, Opcode3, not_3_out, not_4_out, not_5_out, Zero);
  and and_3 (and_3_out, Opcode3, not_6_out, not_7_out, Opcode0, not_8_out);
  and and_4 (and_4_out, Opcode3, not_9_out, Opcode0, not_10_out, Less);
  and and_5 (and_5_out, Opcode3, Opcode1, not_11_out, not_12_out, not_13_out);
  and and_6 (and_6_out, Opcode3, Opcode2, Opcode1, not_14_out);
  and and_7 (OnestoALU, Opcode3, not_15_out);
  or or_1 (IMMtoPC, and_2_out, and_3_out, and_4_out, and_5_out, and_6_out);
endmodule

module Decoder (
  input  [3:0] Opcode,
  input  Subop,
  input  Zero,
  input  Less,
  output ShiftSrc,
  output ShifterToReg,
  output RegWrite,
  output [3:0] ALUOp,
  output IMMtoALU,
  output RegtoPC,
  output IMMtoPC,
  output ZerosToALU,
  output MemWrite,
  output MemtoReg,
  output Halt,
  output LED,
  output WriteLED,
  output MemRead,
  output PCtoReg
);

  wire Arith_LogDecoder_regwrite, comparator_1_eq, comparator_2_eq, JALDecoder_immtopc, JALDecoder_regwrite,
       MemDecoder_regwrite, or_1_out, PCDecoder_immtopc, ShifterDecoder_regwrite;
  wire [3:0] Arith_LogDecoder_aluoperation, multiplexer_1_out, or_3_out, PCDecoder_aluop;

  Comparator #(.width(4), .mode("unsigned")) comparator_1 (
    .a(Opcode), .b(4'b1010), .eq(comparator_1_eq));  // open: gt, lt
  Multiplexer #(.width(4), .enable("false")) multiplexer_1 (
    .in0(Opcode), .in1(4'b1000), .out(multiplexer_1_out), .sel(comparator_1_eq));
  Comparator #(.width(4), .mode("unsigned")) comparator_2 (
    .a(4'b0010), .b(multiplexer_1_out), .eq(comparator_2_eq));  // open: gt, lt
  ShifterDecoder ShifterDecoder (
    .Opcode(multiplexer_1_out), .ShiftSrc(ShiftSrc), .ShiftertoReg(ShifterToReg),
    .RegWrite(ShifterDecoder_regwrite));
  Arith_Log_Decoder Arith_LogDecoder (
    .Opcode(multiplexer_1_out), .Subop(Subop), .ALUOperation(Arith_LogDecoder_aluoperation),
    .RegWrite(Arith_LogDecoder_regwrite), .ALUSrc(IMMtoALU));
  PCDecoder PCDecoder (
    .Opcode(multiplexer_1_out), .Subop(Subop), .Zero(Zero), .Less(Less), .RegtoPC(RegtoPC),
    .IMMtoPC(PCDecoder_immtopc), .ZerosToALU(ZerosToALU), .ALUOp(PCDecoder_aluop));
  MemDecoder MemDecoder (
    .Opcode(multiplexer_1_out), .Subop(Subop), .MemWrite(MemWrite), .MemtoReg(MemtoReg),
    .RegWrite(MemDecoder_regwrite), .MemRead(MemRead));
  HaltDecoder haltdecoder_1 (.Opcode(multiplexer_1_out), .Halt(Halt), .LED(LED));
  PutDecoder PutDecoder (.Opcode(multiplexer_1_out), .WriteLED(WriteLED));
  JALDecoder JALDecoder (
    .Opcode(multiplexer_1_out), .IMMtoPC(JALDecoder_immtopc), .PCtoReg(PCtoReg),
    .RegWrite(JALDecoder_regwrite));
  or or_1 (or_1_out, ShifterDecoder_regwrite, Arith_LogDecoder_regwrite, MemDecoder_regwrite, JALDecoder_regwrite);
  or or_2 (IMMtoPC, PCDecoder_immtopc, JALDecoder_immtopc);
  Multiplexer #(.enable("false")) multiplexer_2 (.in0(or_1_out), .in1(1'b1), .out(RegWrite), .sel(comparator_2_eq));
  assign or_3_out = Arith_LogDecoder_aluoperation | PCDecoder_aluop;  // OR_Gate or_3, 4 bits wide
  Multiplexer #(.width(4), .enable("false")) multiplexer_3 (
    .in0(or_3_out), .in1(4'b1111), .out(ALUOp), .sel(comparator_2_eq));
endmodule

module MemDecoder (
  input  [3:0] Opcode,
  input  Subop,
  output MemWrite,
  output MemtoReg,
  output RegWrite,
  output MemRead
);

  and and_1 (MemWrite, ~Opcode[0], Opcode[1], Opcode[2], ~Opcode[3], Subop);  // AND_Gate
  and and_2 (MemRead, ~Opcode[0], Opcode[1], Opcode[2], ~Opcode[3], ~Subop);  // AND_Gate

  assign MemtoReg = MemRead;
  assign RegWrite = MemRead;
endmodule

module HaltDecoder (
  input  [3:0] Opcode,
  output Halt,
  output LED
);

  and and_1 (Halt, ~Opcode[3], Opcode[2], Opcode[1], Opcode[0]);  // AND_Gate

  assign LED = Halt;
endmodule

module PutDecoder (
  input  [3:0] Opcode,
  output WriteLED
);

  and and_1 (WriteLED, Opcode[0], Opcode[1], Opcode[2], Opcode[3]);
endmodule

module JALDecoder (
  input  [3:0] Opcode,
  output IMMtoPC,
  output PCtoReg,
  output RegWrite
);

  and and_1 (IMMtoPC, ~Opcode[0], ~Opcode[1], Opcode[2], Opcode[3]);  // AND_Gate

  assign PCtoReg = IMMtoPC;
  assign RegWrite = IMMtoPC;
endmodule

module ResultToLess (
  input  [15:0] Result,
  output Less
);


  assign Less = Result[15];
endmodule

module side (
  input  Op3,
  input  Op2,
  input  Op1,
  input  Op0,
  output Op3_2,
  output Op2_2,
  output Op1_2,
  output Op0_2
);

  wire not_1_out;

  and and_1 (Op1_2, Op3, not_1_out);
  not not_1 (not_1_out, Op2);

  assign Op0_2 = 1'b0;
  assign Op2_2 = 1'b0;
  assign Op3_2 = 1'b0;
endmodule

module IF_ID (
  input  [15:0] ReadFromInstMemory,
  input  Freeze,
  input  Clock,
  input  [3:0] op,
  output [15:0] ReadInstruction
);

  Register #(.width(16)) Instruction (
    .D(ReadFromInstMemory), .Q(ReadInstruction), .clk(Clock), .clr(Freeze));  // open: en

  // Notes on the sheet:
  //   IF/ID Register
endmodule

module ID_EX (
  input  ReadFromMemToReg,
  input  ReadFromRegWrite,
  input  HaltLED,
  input  ReadFromMemWrite,
  input  ReadFromMemRead,
  input  [3:0] ReadFromALUOp,
  input  ReadFromImmToALU,
  input  ReadFromImmToPC,
  input  ReadFromZerosToALU,
  input  WriteHex,
  input  [7:0] ImmNotExtended,
  input  [15:0] ReadFromRegData1,
  input  [15:0] WB_WriteData,
  input  [15:0] ReadFromRegData2,
  input  [15:0] ReadFromSignExtend,
  input  [2:0] Rs,
  input  [2:0] Rt,
  input  [2:0] Rd,
  input  WB_RegWrite,
  input  BranchTaken,
  input  Clock,
  output ReadMemToReg,
  output ReadRegWRite,
  output HaltLED_2,
  output ReadMemWrite,
  output MemRead,
  output [3:0] ALUOp,
  output ReadImmToALU,
  output ReadImmToPC,
  output ReadZerosToALU,
  output WriteHex_2,
  output [7:0] ImmNotExtended_2,
  output [15:0] ReadRegData1,
  output [15:0] ReadRegData2,
  output [15:0] ReadSignExtend,
  output [2:0] ReadRs,
  output [2:0] ReadRt,
  output PausePC
);

  wire and_2_out, and_3_out, comparator_1_eq, comparator_2_eq, comparator_3_gt, comparator_4_eq,
       comparator_5_eq, multiplexer_1_out, multiplexer_2_out, multiplexer_3_out, multiplexer_4_out,
       multiplexer_5_out, multiplexer_6_out, multiplexer_9_out, multiplexer_10_out, multiplexer_12_out,
       or_1_out, or_2_out;
  wire [3:0] multiplexer_11_out;
  wire [15:0] multiplexer_7_out, multiplexer_8_out;

  Comparator #(.width(3)) comparator_1 (.a(ReadRs), .b(Rs), .eq(comparator_1_eq));  // open: gt, lt
  Comparator #(.width(3)) comparator_2 (.a(ReadRs), .b(Rt), .eq(comparator_2_eq));  // open: gt, lt
  or or_1 (or_1_out, comparator_1_eq, comparator_2_eq);
  and and_1 (PausePC, MemRead, or_1_out);
  Comparator #(.width(3)) comparator_3 (.a(Rd), .b(3'b000), .gt(comparator_3_gt));  // open: eq, lt
  or or_2 (or_2_out, PausePC, BranchTaken);
  Comparator #(.width(3)) comparator_4 (.a(Rs), .b(Rd), .eq(comparator_4_eq));  // open: gt, lt
  Comparator #(.width(3)) comparator_5 (.a(Rt), .b(Rd), .eq(comparator_5_eq));  // open: gt, lt
  and and_2 (and_2_out, comparator_4_eq, comparator_3_gt, WB_RegWrite);
  and and_3 (and_3_out, comparator_5_eq, comparator_3_gt, WB_RegWrite);
  Multiplexer #(.enable("false")) multiplexer_1 (
    .in0(ReadFromMemToReg), .in1(1'b0), .out(multiplexer_1_out), .sel(or_2_out));
  Multiplexer #(.enable("false")) multiplexer_2 (
    .in0(ReadFromRegWrite), .in1(1'b0), .out(multiplexer_2_out), .sel(or_2_out));
  Multiplexer #(.enable("false")) multiplexer_3 (
    .in0(ReadFromMemWrite), .in1(1'b0), .out(multiplexer_3_out), .sel(or_2_out));
  Multiplexer #(.enable("false")) multiplexer_4 (
    .in0(ReadFromImmToALU), .in1(1'b0), .out(multiplexer_4_out), .sel(or_2_out));
  Multiplexer #(.enable("false")) multiplexer_5 (
    .in0(ReadFromImmToPC), .in1(1'b0), .out(multiplexer_5_out), .sel(or_2_out));
  Multiplexer #(.enable("false")) multiplexer_6 (
    .in0(ReadFromZerosToALU), .in1(1'b0), .out(multiplexer_6_out), .sel(or_2_out));
  Multiplexer #(.width(16), .enable("false")) multiplexer_7 (
    .in0(ReadFromRegData1), .in1(WB_WriteData), .out(multiplexer_7_out), .sel(and_2_out));
  Multiplexer #(.width(16), .enable("false")) multiplexer_8 (
    .in0(ReadFromRegData2), .in1(WB_WriteData), .out(multiplexer_8_out), .sel(and_3_out));
  Multiplexer #(.enable("false")) multiplexer_9 (.in0(HaltLED), .in1(1'b0), .out(multiplexer_9_out), .sel(or_2_out));
  Multiplexer #(.enable("false")) multiplexer_10 (
    .in0(ReadFromMemRead), .in1(1'b0), .out(multiplexer_10_out), .sel(or_2_out));
  Multiplexer #(.width(4), .enable("false")) multiplexer_11 (
    .in0(ReadFromALUOp), .in1(4'b0000), .out(multiplexer_11_out), .sel(or_2_out));
  Multiplexer #(.enable("false")) multiplexer_12 (.in0(WriteHex), .in1(1'b0), .out(multiplexer_12_out), .sel(or_2_out));
  Register Imm (.D(ImmNotExtended), .Q(ImmNotExtended_2), .clk(Clock));  // open: en, clr
  Register #(.width(16)) RegData1 (.D(multiplexer_7_out), .Q(ReadRegData1), .clk(Clock));  // open: en, clr
  Register #(.width(16)) RegData2 (.D(multiplexer_8_out), .Q(ReadRegData2), .clk(Clock));  // open: en, clr
  Register #(.width(16)) SignExtend (.D(ReadFromSignExtend), .Q(ReadSignExtend), .clk(Clock));  // open: en, clr
  Register #(.width(3)) u_Rs (.D(Rs), .Q(ReadRs), .clk(Clock));  // open: en, clr
  Register #(.width(3)) u_Rt (.D(Rt), .Q(ReadRt), .clk(Clock));  // open: en, clr
  Register #(.width(1)) MemToReg (.D(multiplexer_1_out), .Q(ReadMemToReg), .clk(Clock));  // open: en, clr
  Register #(.width(1)) RegWrite (.D(multiplexer_2_out), .Q(ReadRegWRite), .clk(Clock));  // open: en, clr
  Register #(.width(1)) LED (.D(multiplexer_9_out), .Q(HaltLED_2), .clk(Clock));  // open: en, clr
  Register #(.width(1)) MemWrite (.D(multiplexer_3_out), .Q(ReadMemWrite), .clk(Clock));  // open: en, clr
  Register #(.width(1)) u_MemRead (.D(multiplexer_10_out), .Q(MemRead), .clk(Clock));  // open: en, clr
  Register #(.width(4)) u_ALUOp (.D(multiplexer_11_out), .Q(ALUOp), .clk(Clock));  // open: en, clr
  Register #(.width(1)) ImmToALU (.D(multiplexer_4_out), .Q(ReadImmToALU), .clk(Clock));  // open: en, clr
  Register #(.width(1)) ImmToPC (.D(multiplexer_5_out), .Q(ReadImmToPC), .clk(Clock));  // open: en, clr
  Register #(.width(1)) ZerosToALU (.D(multiplexer_6_out), .Q(ReadZerosToALU), .clk(Clock));  // open: en, clr
  Register #(.width(1)) WriteLED (.D(multiplexer_12_out), .Q(WriteHex_2), .clk(Clock));  // open: en, clr

  // Notes on the sheet:
  //   Bubble
  //   MEM
  //   Data
  //   WB
  //   EX
  //   ID/EX Register
endmodule

module EX_MEM (
  input  ReadFromMemToReg,
  input  ReadFromRegWrite,
  input  HaltLED,
  input  ReadFromMemWrite,
  input  ReadFromMemRead,
  input  [15:0] ReadFromRegData1,
  input  [15:0] ReadFromALU,
  input  [15:0] ReadFromRegData2,
  input  [2:0] Rs,
  input  [2:0] Rt,
  input  WriteHex,
  input  Clock,
  output ReadMemToReg,
  output ReadRegWRite,
  output HaltLED_2,
  output ReadMemWrite,
  output MemRead,
  output [15:0] ReadRegData1,
  output [15:0] ALU,
  output [15:0] ReadRegData2,
  output [2:0] ReadRs,
  output [2:0] ReadRt,
  output WriteHex_2
);

  Register #(.width(16)) RegData1 (.D(ReadFromRegData1), .Q(ReadRegData1), .clk(Clock));  // open: en, clr
  Register #(.width(16)) u_ALU (.D(ReadFromALU), .Q(ALU), .clk(Clock));  // open: en, clr
  Register #(.width(16)) RegData2 (.D(ReadFromRegData2), .Q(ReadRegData2), .clk(Clock));  // open: en, clr
  Register #(.width(3)) u_Rs (.D(Rs), .Q(ReadRs), .clk(Clock));  // open: en, clr
  Register #(.width(3)) u_Rt (.D(Rt), .Q(ReadRt), .clk(Clock));  // open: en, clr
  Register #(.width(1)) MemToReg (.D(ReadFromMemToReg), .Q(ReadMemToReg), .clk(Clock));  // open: en, clr
  Register #(.width(1)) RegWrite (.D(ReadFromRegWrite), .Q(ReadRegWRite), .clk(Clock));  // open: en, clr
  Register #(.width(1)) LED (.D(HaltLED), .Q(HaltLED_2), .clk(Clock));  // open: en, clr
  Register #(.width(1)) MemWrite (.D(ReadFromMemWrite), .Q(ReadMemWrite), .clk(Clock));  // open: en, clr
  Register #(.width(1)) u_MemRead (.D(ReadFromMemRead), .Q(MemRead), .clk(Clock));  // open: en, clr
  Register #(.width(1)) MemToReg_2 (.D(WriteHex), .Q(WriteHex_2), .clk(Clock));  // open: en, clr

  // Notes on the sheet:
  //   Data
  //   EX/MEM Register
endmodule

module MEM_WB (
  input  ReadFromMemToReg,
  input  ReadFromRegWrite,
  input  HaltLED,
  input  [15:0] ReadFromALU,
  input  [15:0] MemData,
  input  [2:0] Rs,
  input  [2:0] Rt,
  input  WriteHEx,
  input  [15:0] Data1,
  input  Clock,
  output ReadMemToReg,
  output ReadRegWRite,
  output HaltLED_2,
  output [15:0] ALU,
  output [15:0] MemData_2,
  output [2:0] ReadRs,
  output [2:0] ReadRt,
  output WriteHEx_2,
  output [15:0] Data1_2
);

  Register #(.width(16)) u_ALU (.D(ReadFromALU), .Q(ALU), .clk(Clock));  // open: en, clr
  Register #(.width(16)) u_MemData (.D(MemData), .Q(MemData_2), .clk(Clock));  // open: en, clr
  Register #(.width(3)) u_Rs (.D(Rs), .Q(ReadRs), .clk(Clock));  // open: en, clr
  Register #(.width(3)) u_Rt (.D(Rt), .Q(ReadRt), .clk(Clock));  // open: en, clr
  Register #(.width(16)) u_Data1 (.D(Data1), .Q(Data1_2), .clk(Clock));  // open: en, clr
  Register #(.width(1)) MemToReg (.D(ReadFromMemToReg), .Q(ReadMemToReg), .clk(Clock));  // open: en, clr
  Register #(.width(1)) RegWrite (.D(ReadFromRegWrite), .Q(ReadRegWRite), .clk(Clock));  // open: en, clr
  Register #(.width(1)) LED (.D(HaltLED), .Q(HaltLED_2), .clk(Clock));  // open: en, clr
  Register #(.width(1)) LED_2 (.D(WriteHEx), .Q(WriteHEx_2), .clk(Clock));  // open: en, clr

  // Notes on the sheet:
  //   Data
  //   MEM/WB Register
endmodule

module MemToEx_Forward (
  input  [15:0] IdEx_RsData,
  input  [15:0] ExMemAlu,
  input  [15:0] MemWB_Data,
  input  [2:0] IdEx_Rs,
  input  [2:0] MemWB_Rs,
  input  MemWB_RegWrite,
  input  MemWB_MemToReg,
  input  [2:0] IdEx_Rs_2,
  input  [2:0] ExMem_Rs,
  input  ExMem_RegWrite,
  input  ExMem_MemToReg,
  input  [15:0] IdEx_RtData,
  input  [2:0] IdEx_Rt,
  output [15:0] Rs_Data,
  output [15:0] Rt_Data
);

  wire and_1_out, and_2_out, and_3_out, and_4_out, comparator_1_eq, comparator_2_gt, comparator_3_eq,
       comparator_4_gt, comparator_5_eq, comparator_6_gt, comparator_7_eq, comparator_8_gt;
  wire [15:0] multiplexer_1_out, multiplexer_2_out;

  Comparator #(.width(3), .mode("unsigned")) comparator_1 (
    .a(IdEx_Rs), .b(MemWB_Rs), .eq(comparator_1_eq));  // open: gt, lt
  Comparator #(.width(3), .mode("unsigned")) comparator_2 (
    .a(MemWB_Rs), .b(3'b000), .gt(comparator_2_gt));  // open: eq, lt
  Comparator #(.width(3), .mode("unsigned")) comparator_3 (
    .a(IdEx_Rs_2), .b(ExMem_Rs), .eq(comparator_3_eq));  // open: gt, lt
  Comparator #(.width(3), .mode("unsigned")) comparator_4 (
    .a(ExMem_Rs), .b(3'b000), .gt(comparator_4_gt));  // open: eq, lt
  Comparator #(.width(3), .mode("unsigned")) comparator_5 (
    .a(IdEx_Rt), .b(MemWB_Rs), .eq(comparator_5_eq));  // open: gt, lt
  Comparator #(.width(3), .mode("unsigned")) comparator_6 (
    .a(MemWB_Rs), .b(3'b000), .gt(comparator_6_gt));  // open: eq, lt
  Comparator #(.width(3), .mode("unsigned")) comparator_7 (
    .a(IdEx_Rt), .b(ExMem_Rs), .eq(comparator_7_eq));  // open: gt, lt
  Comparator #(.width(3), .mode("unsigned")) comparator_8 (
    .a(ExMem_Rs), .b(3'b000), .gt(comparator_8_gt));  // open: eq, lt
  and and_1 (and_1_out, ExMem_RegWrite, comparator_3_eq, comparator_4_gt);
  and and_2 (and_2_out, ExMem_RegWrite, comparator_7_eq, comparator_8_gt);
  and and_3 (and_3_out, MemWB_RegWrite, comparator_1_eq, comparator_2_gt);
  and and_4 (and_4_out, MemWB_RegWrite, comparator_5_eq, comparator_6_gt);
  Multiplexer #(.width(16), .enable("false")) multiplexer_1 (
    .in0(IdEx_RsData), .in1(MemWB_Data), .out(multiplexer_1_out), .sel(and_3_out));
  Multiplexer #(.width(16), .enable("false")) multiplexer_2 (
    .in0(IdEx_RtData), .in1(MemWB_Data), .out(multiplexer_2_out), .sel(and_4_out));
  Multiplexer #(.width(16), .enable("false")) multiplexer_3 (
    .in0(multiplexer_1_out), .in1(ExMemAlu), .out(Rs_Data), .sel(and_1_out));
  Multiplexer #(.width(16), .enable("false")) multiplexer_4 (
    .in0(multiplexer_2_out), .in1(ExMemAlu), .out(Rt_Data), .sel(and_2_out));
endmodule

module Halt (
  input  [15:0] Instruction,
  output [3:0] Opcode,
  output Halt
);

  Comparator #(.width(4), .mode("unsigned")) comparator_1 (
    .a(Instruction[15:12]), .b(4'b0111), .eq(Halt));  // open: gt, lt

  assign Opcode = Instruction[15:12];
endmodule

module branchControl (
  input  [3:0] Opcode,
  input  Zero,
  output branch
);

  wire and_1_out, and_2_out, comparator_1_eq, comparator_2_eq, not_1_out;

  Comparator #(.width(4), .mode("unsigned")) comparator_1 (
    .a(Opcode), .b(4'b1010), .eq(comparator_1_eq));  // open: gt, lt
  not not_1 (not_1_out, Zero);
  Comparator #(.width(4), .mode("unsigned")) comparator_2 (
    .a(Opcode), .b(4'b1000), .eq(comparator_2_eq));  // open: gt, lt
  and and_1 (and_1_out, comparator_1_eq, not_1_out);
  and and_2 (and_2_out, Zero, comparator_2_eq);
  or or_1 (branch, and_1_out, and_2_out);
endmodule
